// Logisim project control_logic.circ as structural Verilog: 1 circuit, main circuit control_logic
module control_logic (
  input  [31:0] inst,
  input  BrEq,
  input  BrLt,
  output PCSel,
  output RegWEn,
  output [2:0] ImmSel,
  output BrUn,
  output ASel,
  output BSel,
  output [3:0] ALUSel,
  output MemRW,
  output [1:0] WBSel
);

  wire comparator_1_eq, comparator_2_eq, multiplexer_11_out, not_1_out, not_2_out;
  wire [3:0] ALUSelr_i, ALUSelr_only, multiplexer_2_out;

  Multiplexer #(.select(5), .width(4), .enable("false")) multiplexer_1 (
    .in0(4'b0000), .in1(4'b0110), .in2(4'b0111), .in4(4'b0011), .in5(4'b0100), .in6(4'b0010), .in7(4'b0001),
    .in8(4'b1010), .in9(4'b1110), .in11(4'b1011), .in13(4'b1000), .in15(4'b1001), .in16(4'b1100),
    .in21(4'b0101), .out(ALUSelr_only), .sel({inst[30], inst[25], inst[14:12]}));  // open: in3, in10, in12, in14, in17, in18, in19, in20, in22, in23, in24, in25, in26, in27, in28, in29, in30, in31
  Multiplexer #(.select(5), .width(4), .enable("false")) multiplexer_2 (
    .in0(4'b0000), .in1(4'b0110), .in2(4'b0111), .in4(4'b0011), .in5(4'b0100), .in6(4'b0010), .in7(4'b0001),
    .out(multiplexer_2_out), .sel({2'b00, inst[14:12]}));  // open: in3, in8, in9, in10, in11, in12, in13, in14, in15, in16, in17, in18, in19, in20, in21, in22, in23, in24, in25, in26, in27, in28, in29, in30, in31
  Comparator #(.width(5)) comparator_1 (
    .a(5'b10101), .b({inst[30], inst[25], inst[14:12]}), .eq(comparator_1_eq));  // open: gt, lt
  Multiplexer #(.width(4), .enable("false")) multiplexer_3 (
    .in0(multiplexer_2_out), .in1(4'b0101), .out(ALUSelr_i), .sel(comparator_1_eq));
  Multiplexer #(.select(5), .width(4), .enable("false")) multiplexer_4 (
    .in0(4'b0000), .in4(ALUSelr_i), .in5(4'b0000), .in8(4'b0000), .in12(ALUSelr_only), .in13(4'b0000),
    .in24(4'b0000), .in25(4'b0000), .in27(4'b0000), .out(ALUSel), .sel(inst[6:2]));  // open: in1, in2, in3, in6, in7, in9, in10, in11, in14, in15, in16, in17, in18, in19, in20, in21, in22, in23, in26, in28, in29, in30, in31
  Multiplexer #(.select(5), .width(3), .enable("false")) multiplexer_5 (
    .in0(3'b000), .in4(3'b000), .in5(3'b011), .in8(3'b001), .in13(3'b011), .in24(3'b010), .in25(3'b101),
    .in27(3'b100), .out(ImmSel), .sel(inst[6:2]));  // open: in1, in2, in3, in6, in7, in9, in10, in11, in12, in14, in15, in16, in17, in18, in19, in20, in21, in22, in23, in26, in28, in29, in30, in31
  Multiplexer #(.enable("false")) multiplexer_6 (.in0(1'b1), .in1(1'b0), .out(BSel), .sel(comparator_2_eq));
  Comparator #(.width(5)) comparator_2 (.a(5'b01100), .b(inst[6:2]), .eq(comparator_2_eq));  // open: gt, lt
  Multiplexer #(.select(5), .enable("false")) multiplexer_7 (
    .in0(1'b1), .in4(1'b1), .in5(1'b1), .in8(1'b0), .in12(1'b1), .in13(1'b1), .in24(1'b0), .in25(1'b1),
    .in27(1'b1), .out(RegWEn), .sel(inst[6:2]));  // open: in1, in2, in3, in6, in7, in9, in10, in11, in14, in15, in16, in17, in18, in19, in20, in21, in22, in23, in26, in28, in29, in30, in31
  Multiplexer #(.select(5), .width(2), .enable("false")) multiplexer_8 (
    .in0(2'b00), .in4(2'b01), .in5(2'b01), .in12(2'b01), .in13(2'b01), .in25(2'b10), .in27(2'b10),
    .out(WBSel), .sel(inst[6:2]));  // open: in1, in2, in3, in6, in7, in8, in9, in10, in11, in14, in15, in16, in17, in18, in19, in20, in21, in22, in23, in24, in26, in28, in29, in30, in31
  Comparator #(.width(5)) comparator_3 (.a(5'b01000), .b(inst[6:2]), .eq(MemRW));  // open: gt, lt
  Multiplexer #(.select(5), .enable("false")) multiplexer_9 (
    .in0(1'b0), .in4(1'b0), .in5(1'b1), .in8(1'b0), .in12(1'b0), .in13(1'b0), .in24(1'b1), .in25(1'b0),
    .in27(1'b1), .out(ASel), .sel(inst[6:2]));  // open: in1, in2, in3, in6, in7, in9, in10, in11, in14, in15, in16, in17, in18, in19, in20, in21, in22, in23, in26, in28, in29, in30, in31
  not not_1 (not_1_out, BrLt);
  not not_2 (not_2_out, BrEq);
  Multiplexer #(.select(3), .enable("false")) multiplexer_10 (
    .in0(1'b0), .in1(1'b0), .in4(1'b0), .in5(1'b0), .in6(1'b1), .in7(1'b1), .out(BrUn), .sel(inst[14:12]));  // open: in2, in3
  Multiplexer #(.select(3), .enable("false")) multiplexer_11 (
    .in0(BrEq), .in1(not_2_out), .in4(BrLt), .in5(not_1_out), .in6(BrLt), .in7(not_1_out),
    .out(multiplexer_11_out), .sel(inst[14:12]));  // open: in2, in3
  Multiplexer #(.select(5), .enable("false")) multiplexer_12 (
    .in0(1'b0), .in4(1'b0), .in5(1'b0), .in8(1'b0), .in12(1'b0), .in13(1'b0), .in24(multiplexer_11_out),
    .in25(1'b1), .in27(1'b1), .out(PCSel), .sel(inst[6:2]));  // open: in1, in2, in3, in6, in7, in9, in10, in11, in14, in15, in16, in17, in18, in19, in20, in21, in22, in23, in26, in28, in29, in30, in31

  // Other names for the same wires on the sheet: func3[2:0] = inst[14:12]; func7[1:0] = {inst[30], inst[25]};
  //   opcode[4:0] = inst[6:2]

  // Notes on the sheet:
  //   INPUTS to your circuit
  //   DON'T CHANGE THE LOCATIONS OF THE INPUTS AND OUTPUTS!
  //   OUTPUT from your circuit
endmodule
