// Logisim project cpu.circ as structural Verilog: 1 circuit, main circuit main
module main (
  input  [31:0] INSTRUCTION,
  input  CLOCK,
  output [31:0] PROGRAM_COUNTER,
  output [31:0] ra,
  output [31:0] sp,
  output [31:0] t0,
  output [31:0] t1,
  output [31:0] t2,
  output [31:0] s0,
  output [31:0] s1,
  output [31:0] a0
);

  wire ASel, BrEq, BrLt, BrUn, control_logic_1_bsel, control_logic_1_memrw, control_logic_1_pcsel,
       control_logic_1_regwen, multiplexer_6_out, multiplexer_8_out, select_bit_control, select_bit_swlt;
  wire [1:0] control_logic_1_wbsel;
  wire [2:0] control_logic_1_immsel;
  wire [3:0] control_logic_1_alusel;
  wire [31:0] adder_1_out, adder_2_out, ALUresult, DMEM_p5, multiplexer_1_out, multiplexer_2_out,
       multiplexer_4_out, multiplexer_5_out, multiplexer_7_out, offset, PC_pip, PiP_q, R_rs1, R_rs2,
       swlt_result, WB0;

  control_logic control_logic_1 (
    .BSel(control_logic_1_bsel), .ASel(ASel), .BrUn(BrUn), .ImmSel(control_logic_1_immsel),
    .RegWEn(control_logic_1_regwen), .PCSel(control_logic_1_pcsel), .BrLt(BrLt), .BrEq(BrEq), .inst(PiP_q),
    .ALUSel(control_logic_1_alusel), .MemRW(control_logic_1_memrw), .WBSel(control_logic_1_wbsel));
  Adder #(.width(32)) adder_1 (.a(PROGRAM_COUNTER), .b(32'h4), .out(adder_1_out));  // open: cin, cout
  Multiplexer #(.width(32), .enable("false")) multiplexer_1 (
    .in0(adder_1_out), .in1(ALUresult), .out(multiplexer_1_out), .sel(control_logic_1_pcsel));
  Register #(.width(32)) PC (.D(multiplexer_1_out), .clk(CLOCK), .Q(PROGRAM_COUNTER));  // open: en, clr
  Multiplexer #(.width(32), .enable("false")) multiplexer_2 (
    .in0(INSTRUCTION), .in1(32'h10011), .out(multiplexer_2_out), .sel(control_logic_1_pcsel));
  Register #(.width(32)) PiP (.D(multiplexer_2_out), .clk(CLOCK), .Q(PiP_q));  // open: en, clr
  Register #(.width(32)) register_1 (.D(PROGRAM_COUNTER), .clk(CLOCK), .Q(PC_pip));  // open: en, clr
  Comparator #(.width(32)) comparator_1 (.a(offset), .b(R_rs2), .gt(select_bit_swlt));  // open: eq, lt
  Multiplexer #(.width(32), .enable("false")) multiplexer_3 (
    .in0({32{1'b0}}), .in1(R_rs1), .out(swlt_result), .sel(select_bit_swlt));
  regfile_main RegFile (
    .rs2(PiP_q[24:20]), .rd(PiP_q[11:7]), .Read_Data_1(R_rs1), .Read_Data_2(R_rs2), .ra(ra), .sp(sp),
    .t0(t0), .t1(t1), .t2(t2), .s0(s0), .s1(s1), .a0(a0), .rs1(PiP_q[19:15]), .Write_Data(WB0),
    .RegWEn(control_logic_1_regwen), .clk(CLOCK));
  imm_gen imm_gen_1 (.ImmSel(control_logic_1_immsel), .inst(PiP_q), .imm(offset));
  Multiplexer #(.width(32), .enable("false")) multiplexer_4 (
    .in0(R_rs2), .in1(offset), .out(multiplexer_4_out), .sel(control_logic_1_bsel));
  branch_comp branch_comp_1 (.BrEq(BrEq), .rs1(R_rs1), .rs2(R_rs2), .BrLt(BrLt), .BrUn(BrUn));
  Multiplexer #(.width(32), .enable("false")) multiplexer_5 (
    .in0(R_rs1), .in1(PC_pip), .out(multiplexer_5_out), .sel(ASel));
  alu Arithmetic_Logic_Unit (
    .ALUSel(control_logic_1_alusel), .Result(ALUresult), .A(multiplexer_5_out), .B(multiplexer_4_out));
  Multiplexer #(.enable("false")) multiplexer_6 (
    .in0(control_logic_1_memrw), .in1(multiplexer_8_out), .out(multiplexer_6_out), .sel(select_bit_control));
  Comparator comparator_2 (
    .a(8'he8), .b({INSTRUCTION[14:12], INSTRUCTION[6:2]}), .eq(select_bit_control));  // open: gt, lt
  Multiplexer #(.width(32), .enable("false")) multiplexer_7 (
    .in0(ALUresult), .in1(swlt_result), .out(multiplexer_7_out), .sel(select_bit_control));
  Multiplexer #(.enable("false")) multiplexer_8 (
    .in0(1'b0), .in1(1'b1), .out(multiplexer_8_out), .sel(select_bit_swlt));
  // mem_main DMEM: pin names not known; wires that end beside it: multiplexer_7_out, R_rs2, CLOCK, multiplexer_6_out, DMEM_p5
  Adder #(.width(32)) adder_2 (.a(PC_pip), .b(32'h4), .out(adder_2_out));  // open: cin, cout
  Multiplexer #(.select(2), .width(32), .enable("false")) multiplexer_9 (
    .in0(DMEM_p5), .in1(ALUresult), .in2(adder_2_out), .out(WB0), .sel(control_logic_1_wbsel));  // open: in3

  // Other names for the same wires on the sheet: clk = CLOCK;
  //   opcode_funct3[7:0] = {INSTRUCTION[14:12], INSTRUCTION[6:2]}

  // Notes on the sheet:
  //   Output
  //   IMEM (do **NOT** move this)
  //   Inputs
  //   Inputs/Outputs for testing. Do **NOT** move these.
endmodule
