// Logisim project imm_gen.circ as structural Verilog: 1 circuit, main circuit imm_gen
module imm_gen (
  input  [31:0] inst,
  input  [2:0] ImmSel,
  output [31:0] imm
);

  wire [31:0] I_type_jalr, itype_i_lw, S_type, SB_type, UJ_type;

  assign I_type_jalr = {{20{inst[31]}}, inst[31:20]};  // Bit_Extender bit_extender_1
  assign itype_i_lw = {{20{inst[31]}}, inst[31:20]};  // Bit_Extender bit_extender_2
  assign S_type = {{20{inst[31]}}, {inst[31:25], inst[11:7]}};  // Bit_Extender bit_extender_3
  assign SB_type = {{19{inst[31]}}, {inst[31], inst[7], inst[30:25], inst[11:8], 1'b0}};  // Bit_Extender bit_extender_4
  assign UJ_type = {{11{inst[31]}}, {inst[31], inst[19:12], inst[20], inst[30:21], 1'b0}};  // Bit_Extender bit_extender_5
  Multiplexer #(.select(3), .width(32), .enable("false")) multiplexer_1 (
    .in0(itype_i_lw), .in1(S_type), .in2(SB_type), .in3({inst[31:12], {12{1'b0}}}), .in4(UJ_type),
    .in5(I_type_jalr), .out(imm), .sel(ImmSel));  // open: in6, in7

  // Other names for the same wires on the sheet: one_four[3:0] = inst[11:8]; eleventh = inst[7];
  //   one_ten_1[9:0] = inst[30:21]; U_type[31:12] = inst[31:12]; five_ten[5:0] = inst[30:25]; eleventh_1 = inst[20];
  //   twelve_ninteen_1[7:0] = inst[19:12]; twelve = inst[31]; twenty_1 = inst[31]

  // Notes on the sheet:
  //   INPUTS to your circuit
  //   DON'T CHANGE THE LOCATIONS OF THE INPUTS AND OUTPUTS!
  //   OUTPUT from your circuit
endmodule
